# Fritzing sketch Nano-HC06-ESC-Servo (saved by Fritzing 0.9.3b)
breadboards: 1

parts:
  Part1 = Arduino Nano (Rev3.0)
  Part2 = Bluetooth HC-06
  M1 = ESC
  920KV_Motor1 = DJI 920 KV Motor
  Power_plug1 = Power plug  # not connected
  J1 = Basic Servo

nets:
  N1: Part1.D1/TX, Part2.RXD
  N2: Part1.D0/RX, Part2.TXD
  GND: Part1.GND, Part2.GND, M1.GND, J1.gnd
  N3: Part1.D10, M1.DATA
  N4: Part1.D11/MOSI, J1.pulse
  VCC: Part1.VIN, Part2.VCC, M1.pin_8, J1.vcc
  N5: M1.U, 920KV_Motor1.u
  N6: M1.V, 920KV_Motor1.v
  N7: M1.W, 920KV_Motor1.w

custom parts:
  DJI 920 KV Motor: DJI Brushless Outrunner 2212/920K Motor F330-550
