# Fritzing sketch Nano-HC06-config (saved by Fritzing 0.9.3b)
breadboards: 1

parts:
  Part1 = Arduino Nano (Rev3.0)
  Part2 = Bluetooth HC-06

nets:
  GND: Part1.GND, Part2.GND
  N1: Part1.D10, Part2.TXD
  N2: Part1.D11/MOSI, Part2.RXD
  5V: Part1.5V, Part2.VCC
