# Fritzing sketch ESP32-CRSERVO (saved by Fritzing 0.9.3b)
breadboards: 1

parts:
  MCU1 = Wemos Lolin32lite
  Right_motor = Basic Servo
  Left_motor = Basic Servo
  U1 = LIPO-110mAh [package=lipo-110]

nets:
  N1: MCU1.pin_6, Right_motor.pulse
  N2: MCU1.pin_7, Left_motor.pulse
  GND: MCU1.pin_13, Right_motor.gnd, Left_motor.gnd
  N3: MCU1.pin_14, U1.+
  N4: MCU1.pin_15, U1.-
  VCC: Right_motor.vcc, Left_motor.vcc

custom parts:
  Wemos Lolin32lite: Wemos Lolinlite32 wifi and blue tooth board based on the ESP-32 cpu, digital I/Os 19, analog inputs 6, clock 240mhz, Flash 4Mbytes, lipo battery charger (500ma connection broken out on breadboard but not pcb), usb.
