# Fritzing sketch ESP32-ESC (saved by Fritzing 0.9.3b)
breadboards: 1

parts:
  MCU1 = Wemos Lolin32lite
  Rudder_Servo = Basic Servo
  U1 = LIPO-110mAh [package=lipo-110]
  M2 = ESC
  Prop_Motor = DJI 920 KV Motor
  2S_LIPO = Power plug  # not connected

nets:
  N1: MCU1.pin_6, M2.DATA
  N2: MCU1.pin_7, Rudder_Servo.pulse
  GND: MCU1.pin_13, Rudder_Servo.gnd, M2.GND
  N3: MCU1.pin_14, U1.+
  N4: MCU1.pin_15, U1.-
  N5: Rudder_Servo.vcc, M2.pin_8
  N6: M2.U, Prop_Motor.u
  N7: M2.V, Prop_Motor.v
  N8: M2.W, Prop_Motor.w

custom parts:
  Wemos Lolin32lite: Wemos Lolinlite32 wifi and blue tooth board based on the ESP-32 cpu, digital I/Os 19, analog inputs 6, clock 240mhz, Flash 4Mbytes, lipo battery charger (500ma connection broken out on breadboard but not pcb), usb.
  DJI 920 KV Motor: DJI Brushless Outrunner 2212/920K Motor F330-550
