# Fritzing sketch nano-BT-ESC (saved by Fritzing 0.9.3b)
breadboards: 1

parts:
  Rudder_Servo = Basic Servo
  M2 = ESC
  Prop_Motor = DJI 920 KV Motor
  2S_LIPO = Power plug  # not connected
  Part1 = Arduino Nano (Rev3.0) (ICSP)
  Part2 = Bluetooth HC-06

nets:
  GND: Rudder_Servo.gnd, M2.GND, Part1.GND, Part2.GND
  VCC: Rudder_Servo.vcc, M2.pin_8, Part1.VIN, Part2.VCC
  N1: Rudder_Servo.pulse, Part1.D6
  N2: M2.U, Prop_Motor.u
  N3: M2.V, Prop_Motor.v
  N4: M2.W, Prop_Motor.w
  N5: M2.DATA, Part1.D5
  N6: Part1.D1/TX, Part2.RXD
  N7: Part1.D0/RX, Part2.TXD

custom parts:
  DJI 920 KV Motor: DJI Brushless Outrunner 2212/920K Motor F330-550
