# Fritzing sketch nano-BT-crservo (saved by Fritzing 0.9.3b)
breadboards: 1

parts:
  Right_Motor = Basic Servo
  M2 = ESC
  2S_LIPO = Power plug  # not connected
  Part1 = Arduino Nano (Rev3.0) (ICSP)
  Part2 = Bluetooth HC-06
  Left_Motor = Basic Servo

nets:
  GND: Right_Motor.gnd, M2.GND, Part1.GND, Part2.GND, Left_Motor.gnd
  VCC: Right_Motor.vcc, M2.pin_8, Part1.VIN, Part2.VCC, Left_Motor.vcc
  N1: Right_Motor.pulse, Part1.D6
  N2: Part1.D1/TX, Part2.RXD
  N3: Part1.D0/RX, Part2.TXD
  N4: Part1.D5, Left_Motor.pulse
